// Logisim project 1bit_cpu.circ as structural Verilog: 1 circuit, main circuit main
module main (
  input  in_1,
  output out_2
);

  wire not_1_out;

  not not_1 (not_1_out, out_2);
  D_Flip_Flop d_ff_1 (.D(not_1_out), .clk(in_1), .Q(out_2));  // open: Qn, preset, reset
endmodule
