// Logisim project 2registers.circ as structural Verilog: 1 circuit, main circuit main
module main (
  input  in_1,
  input  in_2,
  output out_3,
  output out_4
);

  wire A2_q, B_q;

  D_Flip_Flop A (.D(B_q), .clk(in_1), .Q(out_3));  // open: Qn, preset, reset
  D_Flip_Flop B (.D(B_q), .clk(in_1), .Q(B_q));  // open: Qn, preset, reset
  D_Flip_Flop A2 (.D(A2_q), .clk(in_2), .Q(A2_q));  // open: Qn, preset, reset
  D_Flip_Flop B2 (.D(A2_q), .clk(in_2), .Q(out_4));  // open: Qn, preset, reset

  // Notes on the sheet:
  //   MOV A, B
  //   MOV B, A
endmodule
