// Logisim project td4_cpu.circ as structural Verilog: 3 circuits, main circuit main
module main (
  input  in_1,
  input  IM_1,
  input  IM_2,
  input  in_4,
  input  IM_3,
  input  IM_4,
  input  in_7,
  input  in_8,
  input  CK,
  input  A,
  input  B,
  input  in_12,
  input  in_13,
  input  in_14,
  input  in_15,
  input  in_16,
  input  in_17,
  input  in_18,
  input  in_19,
  input  in_20,
  input  in_21,
  input  in_22
);

  wire counter_2_p1, counter_2_p2, counter_2_p3, counter_2_p4, counter_3_p1, counter_3_p2, counter_3_p3,
       counter_3_p4, custom_74hc161_1_qa, custom_74hc161_1_qb, custom_74hc161_1_qc, custom_74hc161_1_qd,
       custom_74hc161_2_qa, custom_74hc161_2_qb, custom_74hc161_2_qc, custom_74hc161_2_qd,
       custom_74hc161_3_qa, custom_74hc161_3_qb, custom_74hc161_3_qc, custom_74hc161_3_qd,
       custom_74hc283_1_c4, custom_74hc283_1_s1, custom_74hc283_1_s2, custom_74hc283_1_s3,
       custom_74hc283_1_s4, custom_74hc283_2_c4, custom_74hc283_2_s1, custom_74hc283_2_s2,
       custom_74hc283_2_s3, custom_74hc283_2_s4, multiplexer_1_out, multiplexer_2_out, multiplexer_3_out,
       multiplexer_4_out, multiplexer_5_out, multiplexer_6_out, multiplexer_7_out, multiplexer_8_out,
       undriven, undriven_2, undriven_3;
  wire [3:0] counter_1_q;

  Counter #(.max('hf), .width(4)) counter_1 (.Q(counter_1_q));  // open: clr, load, up, count, clk, D, carry
  // Counter #(.max('hf), .width(4)) counter_2: pin names not known; wires that end beside it: counter_2_p1, counter_2_p2, counter_2_p3, counter_2_p4
  // Counter #(.max('hf), .width(4)) counter_3: pin names not known; wires that end beside it: counter_3_p1, counter_3_p2, counter_3_p3, counter_3_p4
  Counter #(.max('hf), .width(4)) counter_4 ();  // open: clr, load, up, count, clk, D, carry, Q
  custom_74HC161 custom_74hc161_1 (
    .A(custom_74hc283_2_s1), .B(custom_74hc283_2_s2), .C(custom_74hc283_2_s3), .D(custom_74hc283_2_s4),
    .LD(in_12), .CK(in_20), .QA(custom_74hc161_1_qa), .QB(custom_74hc161_1_qb), .QC(custom_74hc161_1_qc),
    .QD(custom_74hc161_1_qd));
  custom_74HC161 custom_74hc161_2 (
    .A(custom_74hc283_2_s1), .B(custom_74hc283_2_s2), .C(custom_74hc283_2_s3), .D(custom_74hc283_2_s4),
    .LD(in_15), .CK(in_20), .QA(custom_74hc161_2_qa), .QB(custom_74hc161_2_qb), .QC(custom_74hc161_2_qc),
    .QD(custom_74hc161_2_qd));
  custom_74HC161 custom_74hc161_3 (
    .A(custom_74hc283_2_s1), .B(custom_74hc283_2_s2), .C(custom_74hc283_2_s3), .D(custom_74hc283_2_s4),
    .LD(in_18), .CK(in_20), .QA(custom_74hc161_3_qa), .QB(custom_74hc161_3_qb), .QC(custom_74hc161_3_qc),
    .QD(custom_74hc161_3_qd));
  custom_74HC161 custom_74hc161_4 (
    .A(custom_74hc283_2_s1), .B(custom_74hc283_2_s2), .C(custom_74hc283_2_s3), .D(custom_74hc283_2_s4),
    .LD(in_19), .CK(in_20));  // open: QA, QB, QC, QD
  Multiplexer #(.select(2)) multiplexer_1 (
    .in0(counter_1_q[0]), .in1(counter_2_p1), .in2(counter_3_p1), .in3(1'b0), .out(multiplexer_1_out),
    .sel({B, A}));
  Multiplexer #(.select(2)) multiplexer_2 (
    .in0(counter_1_q[2]), .in1(counter_2_p2), .in2(counter_3_p2), .in3(1'b0), .out(multiplexer_2_out),
    .sel({B, A}));
  Multiplexer #(.select(2)) multiplexer_3 (
    .in0(undriven), .in1(counter_2_p3), .in2(counter_3_p3), .in3(1'b0), .out(multiplexer_3_out), .sel({B, A}));
  Multiplexer #(.select(2)) multiplexer_4 (
    .in0(undriven_2), .in1(counter_2_p4), .in2(counter_3_p4), .in3(1'b0), .out(multiplexer_4_out),
    .sel({2{A}}));
  Multiplexer #(.select(2)) multiplexer_5 (
    .in0(custom_74hc161_1_qa), .in1(custom_74hc161_2_qa), .in2(custom_74hc161_3_qa), .in3(1'b0),
    .out(multiplexer_5_out), .sel({in_22, in_21}));
  Multiplexer #(.select(2)) multiplexer_6 (
    .in0(custom_74hc161_1_qb), .in1(custom_74hc161_2_qb), .in2(custom_74hc161_3_qb), .in3(1'b0),
    .out(multiplexer_6_out), .sel({in_22, in_21}));
  Multiplexer #(.select(2)) multiplexer_7 (
    .in0(custom_74hc161_1_qc), .in1(custom_74hc161_2_qc), .in2(custom_74hc161_3_qc), .in3(1'b0),
    .out(multiplexer_7_out), .sel({in_22, in_21}));
  Multiplexer #(.select(2)) multiplexer_8 (
    .in0(custom_74hc161_1_qd), .in1(custom_74hc161_2_qd), .in2(custom_74hc161_3_qd), .in3(1'b0),
    .out(multiplexer_8_out), .sel({2{in_21}}));
  custom_74HC283 custom_74hc283_1 (
    .A1(multiplexer_1_out), .B1(IM_1), .A2(multiplexer_2_out), .B2(IM_2), .A3(multiplexer_3_out), .B3(IM_3),
    .A4(multiplexer_4_out), .B4(IM_4), .S1(custom_74hc283_1_s1), .S2(custom_74hc283_1_s2),
    .S3(custom_74hc283_1_s3), .S4(custom_74hc283_1_s4), .C4(custom_74hc283_1_c4));
  custom_74HC283 custom_74hc283_2 (
    .A1(multiplexer_5_out), .B1(in_13), .A2(multiplexer_6_out), .B2(in_14), .A3(multiplexer_7_out),
    .B3(in_16), .A4(multiplexer_8_out), .B4(in_17), .S1(custom_74hc283_2_s1), .S2(custom_74hc283_2_s2),
    .S3(custom_74hc283_2_s3), .S4(custom_74hc283_2_s4), .C4(custom_74hc283_2_c4));
  D_Flip_Flop d_ff_1 (.D(custom_74hc283_1_c4), .clk(undriven_3));  // open: Q, Qn, preset, reset
  D_Flip_Flop d_ff_2 (.D(custom_74hc283_2_c4), .clk(in_20));  // open: Q, Qn, preset, reset
endmodule

module custom_74HC161 (
  input  A,
  input  B,
  input  C,
  input  D,
  input  LD,
  input  CK,
  output QA,
  output QB,
  output QC,
  output QD
);

  wire d_ff_1_qn, multiplexer_1_out, multiplexer_2_out, multiplexer_3_out, multiplexer_4_out, not_1_out;

  Multiplexer multiplexer_1 (.in0(QA), .in1(A), .out(multiplexer_1_out), .sel(not_1_out));
  Multiplexer multiplexer_2 (.in0(QB), .in1(B), .out(multiplexer_2_out), .sel(not_1_out));
  Multiplexer multiplexer_3 (.in0(QC), .in1(C), .out(multiplexer_3_out), .sel(not_1_out));
  Multiplexer multiplexer_4 (.in0(QD), .in1(D), .out(multiplexer_4_out), .sel(not_1_out));
  not not_1 (not_1_out, LD);
  D_Flip_Flop d_ff_1 (.D(multiplexer_1_out), .clk(CK), .Q(QA), .Qn(d_ff_1_qn));  // open: preset, reset
  D_Flip_Flop d_ff_2 (.D(multiplexer_2_out), .clk(CK), .Q(QB));  // open: Qn, preset, reset
  D_Flip_Flop d_ff_3 (.D(multiplexer_3_out), .clk(CK), .Q(QC));  // open: Qn, preset, reset
  D_Flip_Flop d_ff_4 (.D(multiplexer_4_out), .clk(CK), .Q(QD));  // open: Qn, preset, reset
endmodule

module custom_74HC283 (
  input  A1,
  input  B1,
  input  A2,
  input  B2,
  input  A3,
  input  B3,
  input  A4,
  input  B4,
  output S1,
  output S2,
  output S3,
  output S4,
  output C4
);

  wire adder_1_cout, adder_2_cout, adder_3_cout;

  Adder #(.width(1)) adder_1 (.a(A1), .b(B1), .out(S1), .cout(adder_1_cout));  // open: cin
  Adder #(.width(1)) adder_2 (.a(A2), .b(B2), .out(S2), .cin(adder_1_cout), .cout(adder_2_cout));
  Adder #(.width(1)) adder_3 (.a(A3), .b(B3), .out(S3), .cin(adder_2_cout), .cout(adder_3_cout));
  Adder #(.width(1)) adder_4 (.a(A4), .b(B4), .out(S4), .cin(adder_3_cout), .cout(C4));
endmodule
