// Logisim project temp.circ as structural Verilog: 1 circuit, main circuit main
module main (
  input  in_1,
  input  C0,
  input  C1,
  input  C2,
  input  C3,
  input  A,
  input  in_7,
  input  B,
  input  in_9,
  input  in_10,
  input  [1:0] in_11,
  input  in_12,
  input  in_13,
  input  in_14,
  input  in_15,
  input  in_16,
  input  in_17,
  input  in_18,
  input  in_19,
  input  count_0_load_1,
  input  incre_for_1,
  input  count_enable_on_1,
  input  in_23,
  input  in_24,
  output out_25,
  output out_26,
  output out_27,
  output out_28,
  output out_29,
  output out_30,
  output out_31,
  output out_32,
  output out_33,
  output out_34,
  output out_35,
  output out_36,
  output out_37,
  output out_38,
  output out_39
);

  wire and_1_out, and_2_out, and_3_out, and_5_out, d_ff_1_q, d_ff_2_q, multiplexer_1_out, not_1_out,
       not_2_out, not_3_out, xor_2_out;
  wire [3:0] counter_1_q;
  wire [3:1] undriven;

  not not_1 (not_1_out, d_ff_1_q);
  D_Flip_Flop d_ff_1 (.D(not_1_out), .clk(in_1), .Q(d_ff_1_q));  // open: Qn, preset, reset
  D_Flip_Flop d_ff_2 (.D(multiplexer_1_out), .clk(in_7), .Q(d_ff_2_q));  // open: Qn, preset, reset
  not not_2 (not_2_out, in_13);
  not not_3 (not_3_out, d_ff_2_q);
  and and_1 (and_1_out, in_10, in_13);
  and and_2 (and_2_out, in_12, not_2_out);
  and and_3 (and_3_out, in_17, in_18);
  Multiplexer multiplexer_1 (.in0(d_ff_2_q), .in1(not_3_out), .out(multiplexer_1_out), .sel(in_9));
  or or_1 (out_28, and_1_out, and_2_out);
  xor xor_1 (out_35, in_14, in_15);
  and and_4 (out_36, in_14, in_15);
  xor xor_2 (xor_2_out, in_17, in_18);
  Counter #(.max('hf), .width(4)) counter_1 (
    .clr(in_19), .load(count_0_load_1), .up(incre_for_1), .count(count_enable_on_1), .clk(in_23),
    .D({undriven, in_24}), .carry(out_39), .Q(counter_1_q));
  xor xor_3 (out_37, in_16, xor_2_out);
  and and_5 (and_5_out, in_16, xor_2_out);
  or or_2 (out_38, and_5_out, and_3_out);
  ROM #(.addrWidth(2)) rom_1 (.addr(in_11), .data({out_34, out_33, out_32, out_31, out_30, out_29, out_27, out_26}));
  Multiplexer #(.select(2)) multiplexer_2 (.in0(C0), .in1(C1), .in2(C2), .in3(C3), .out(out_25), .sel({B, A}));

  // Notes on the sheet:
  //   contents of rom_1 (hex, n*v repeats v):
  //   d5
endmodule
