// Logisim project xor.circ as structural Verilog: 1 circuit, main circuit main
module main (
  input  in_1,
  input  in_2,
  output out_3
);

  wire And1_out, And2_out, not_1_out, not_2_out;

  not not_1 (not_1_out, in_2);
  not not_2 (not_2_out, in_1);
  and And1 (And1_out, in_1, not_1_out);
  and And2 (And2_out, not_2_out, in_2);
  or Or1 (out_3, And1_out, And2_out);
endmodule
